// Logisim project part1.circ as structural Verilog: 8 circuits, main circuit MyTest
module MyTest (
);

  wire AND_out, not_1_out, undriven, undriven_2;

  and AND (AND_out, undriven, undriven_2);
  not not_1 (not_1_out, AND_out);

  // Notes on the sheet:
  //   INPUT1
  //   INPUT2
  //   NOT
endmodule

module NAND1 (
  input  in_1,
  input  in_2,
  input  in_3,
  input  in_4,
  output out_5,
  output out_6
);

  wire and_1_out;

  and and_1 (and_1_out, in_3, in_4);
  not not_1 (out_6, and_1_out);

  // Other names for the same wires on the sheet: Result = out_5; X = in_1; Y = in_2

  // Notes on the sheet:
  //   ------------------------------------------ Put your circuit below this line ------------------
endmodule

module NOR1 (
  input  in_1,
  input  in_2,
  input  in_3,
  input  in_4,
  output out_5,
  output out_6
);

  wire or_1_out;

  or or_1 (or_1_out, in_3, in_4);
  not not_1 (out_6, or_1_out);

  // Other names for the same wires on the sheet: Result = out_5; X = in_1; Y = in_2

  // Notes on the sheet:
  //   ------------------------------------------ Put your circuit below this line ------------------
endmodule

module XOR1 (
  input  in_1,
  input  in_2,
  input  in_3,
  input  in_4,
  output out_5,
  output out_6
);

  wire and_1_out, and_2_out, not_1_out, not_2_out;

  not not_1 (not_1_out, in_4);
  not not_2 (not_2_out, in_3);
  and and_1 (and_1_out, in_3, not_1_out);
  and and_2 (and_2_out, not_2_out, in_4);
  or or_1 (out_6, and_1_out, and_2_out);

  // Other names for the same wires on the sheet: Result = out_5; X = in_1; Y = in_2

  // Notes on the sheet:
  //   ------------------------------------------ Put your circuit below this line ------------------
endmodule

module Mux2to1 (
  input  in_1,
  input  in_2,
  input  in_3,
  input  in_4,
  input  A,
  input  in_6,
  output out_7,
  output out_8
);

  wire and_1_out, and_2_out, and_3_out, and_4_out, not_1_out, not_2_out, not_3_out;

  and and_1 (and_1_out, A, A);
  not not_1 (not_1_out, and_1_out);
  not not_2 (not_2_out, and_2_out);
  and and_2 (and_2_out, in_4, A);
  and and_3 (and_3_out, not_1_out, in_6);
  not not_3 (not_3_out, and_3_out);
  not not_4 (out_8, and_4_out);
  and and_4 (and_4_out, not_2_out, not_3_out);

  // Other names for the same wires on the sheet: Result = out_7; S = in_3; X = in_1; Y = in_2

  // Notes on the sheet:
  //   ------------------------------------------ Put your circuit below this line ------------------
endmodule

module Dec2to4 (
  input  [1:0] in_1,
  input  A,
  input  A_2,
  output [3:0] out_4,
  output out_5,
  output out_6,
  output out_7,
  output out_8
);

  wire not_1_out, not_2_out;

  not not_1 (not_1_out, A);
  not not_2 (not_2_out, A_2);
  and and_1 (out_5, not_1_out, not_2_out);
  and and_2 (out_6, not_2_out, A);
  and and_3 (out_7, not_1_out, A_2);
  and and_4 (out_8, A_2, A);

  // Other names for the same wires on the sheet: Result[3:0] = out_4; S[1:0] = in_1

  // Notes on the sheet:
  //   S is decoder's 2-bit inputs
  //   ------------------------------------------ Put your circuit below this line ------------------
  //   Result is decoder's 4-bit outputs
endmodule

module Mux4to1 (
  input  in_1,
  input  in_2,
  input  in_3,
  input  in_4,
  input  [1:0] in_5,
  input  in_6,
  input  in_7,
  input  in_8,
  input  in_9,
  input  A,
  input  A_2,
  output out_12,
  output out_13
);

  wire and_1_out, and_2_out, and_3_out, and_4_out, and_5_out, and_6_out, and_7_out, not_1_out, not_2_out,
       not_3_out, not_4_out, not_5_out, not_6_out;

  not not_1 (not_1_out, and_1_out);
  and and_1 (and_1_out, A, A);
  and and_2 (and_2_out, A_2, A_2);
  not not_2 (not_2_out, and_2_out);
  and and_3 (and_3_out, in_6, not_1_out, not_2_out);
  and and_4 (and_4_out, in_7, not_1_out, A_2);
  and and_5 (and_5_out, in_8, A, not_2_out);
  and and_6 (and_6_out, in_9, A, A_2);
  not not_3 (not_3_out, and_3_out);
  not not_4 (not_4_out, and_4_out);
  not not_5 (not_5_out, and_5_out);
  not not_6 (not_6_out, and_6_out);
  and and_7 (and_7_out, not_3_out, not_4_out, not_5_out, not_6_out);
  not not_7 (out_13, and_7_out);

  // Other names for the same wires on the sheet: A_t = in_1; B = in_2; C = in_3; D = in_4; Result = out_12;
  //   S[1:0] = in_5

  // Notes on the sheet:
  //   S=00 selects A
  //   S=01 selects B
  //   S=10 selects C
  //   S=11 selects D
  //   ------------------------------------------ Put your circuit below this line ------------------
endmodule

module NegSign (
  input  [7:0] in_1,
  input  in_2,
  input  in_3,
  input  in_4,
  input  in_5,
  input  in_6,
  input  in_7,
  input  in_8,
  input  in_9,
  input  [7:0] in_10,
  output [7:0] out_11,
  output out_12,
  output out_13,
  output out_14,
  output out_15,
  output out_16,
  output out_17,
  output out_18,
  output out_19,
  output [7:0] out_20
);

  not not_1 (out_12, in_2);
  not not_2 (out_13, in_3);
  not not_3 (out_14, in_4);
  not not_4 (out_15, in_5);
  not not_5 (out_16, in_6);
  not not_6 (out_17, in_7);
  not not_7 (out_18, in_8);
  not not_8 (out_19, in_9);
  assign out_20 = ~in_10;  // NOT_Gate not_9, 8 bits wide

  // Other names for the same wires on the sheet: Result[7:0] = out_11; X[7:0] = in_1

  // Notes on the sheet:
  //   ------------------------------------------ Put your circuit below this line ------------------
endmodule
